# Fritzing sketch TetrisFritzing (saved by Fritzing 0.8.7b)
breadboards: 1

parts:
  Raspberry_Pi_1 = Raspberry Pi 3
  S1 = Round Pushbutton
  S2 = Round Pushbutton
  S3 = Round Pushbutton

nets:
  N1: Raspberry_Pi_1.3v3, S1.leg1, S2.leg1, S3.leg1
  N2: Raspberry_Pi_1.GIPO19, S2.leg0
  N3: Raspberry_Pi_1.GIPO24, S3.leg0
  N4: Raspberry_Pi_1.GIPO18, S1.leg0
